# Fritzing sketch 1008_5 (saved by Fritzing 1.0.3b)
breadboards: 1

parts:
  パーツ3 = Arduino Uno (Rev3) - ICSP
  LED3 = smd LED [color="Red (633nm)" package="0603 [SMD]"]
  R2 = Resistor [tolerance=±5% power=0.25W resistance=1k package=THT]
  S3 = Pushbutton [package="[THT]"]
  LED4 = smd LED [color="Red (633nm)" package="0603 [SMD]"]
  R1 = Resistor [tolerance=±5% power=0.25W resistance=1k package=THT]

nets:
  N1: パーツ3.D8, R2.Pin_1
  N2: パーツ3.D9_PWM, R1.Pin_1
  N3: パーツ3.GND, LED3.cathode, S3.Pin_1, S3.Pin_2, LED4.cathode
  N4: パーツ3.D7, S3.Pin_3, S3.Pin_4
  N5: LED3.anode, R1.Pin_0
  N6: R2.Pin_0, LED4.anode
